// Logisim project Banco_de_registradores_4x8.circ as structural Verilog: 5 circuits, main circuit main
module main (
);

  wire adder_1_cout;
  wire [1:0] intruct_1_r1, intruct_1_r2;
  wire [2:0] Ula_Op;
  wire [3:0] intruct_1_imm, intruct_1_opcode;
  wire [7:0] adder_1_out, bit_extender_1_out, multiplexer_1_out, PC_q, regbank_1_inf_a, regbank_1_inf_b;

  Register PC (.D(adder_1_out), .en(1'b1), .Q(PC_q));  // open: clk, clr
  Adder adder_1 (.a(8'h4), .b(PC_q), .out(adder_1_out), .cin(1'b0), .cout(adder_1_cout));
  Dual_port_RAM dual_port_ram_1 ();  // open: addr, pc, d, w, instr, data
  intruct intruct_1 (
    .opcode(intruct_1_opcode), .R1(intruct_1_r1), .R2(intruct_1_r2), .imm(intruct_1_imm));  // open: Inst, Type_I
  ROM #(.addrWidth(4)) Control_mem (.addr(intruct_1_opcode));  // open: data
  assign bit_extender_1_out = {{4{intruct_1_imm[3]}}, intruct_1_imm};  // Bit_Extender bit_extender_1
  RegBank regbank_1 (
    .Ra(intruct_1_r1), .Rb(intruct_1_r2), .Inf_a(regbank_1_inf_a), .Inf_b(regbank_1_inf_b));  // open: WriteBack, WE, CLK
  Multiplexer #(.width(8)) multiplexer_1 (
    .in0(regbank_1_inf_b), .in1(bit_extender_1_out), .out(multiplexer_1_out));  // open: sel
  ULA ula_1 (.Ula_op(Ula_Op), .Ra(regbank_1_inf_a), .Rb(multiplexer_1_out));  // open: zero, ULA_out
endmodule

module RegBank (
  input  [7:0] WriteBack,
  input  [1:0] Ra,
  input  [1:0] Rb,
  input  WE,
  input  CLK,
  output [7:0] Inf_a,
  output [7:0] Inf_b
);

  wire demultiplexer_2_out0, demultiplexer_2_out1, demultiplexer_2_out2, demultiplexer_2_out3;
  wire [7:0] demultiplexer_1_out0, demultiplexer_1_out1, demultiplexer_1_out2, demultiplexer_1_out3, R0, R1,
       R2, R3;

  Demultiplexer #(.select(2), .width(8)) demultiplexer_1 (
    .out0(demultiplexer_1_out0), .out1(demultiplexer_1_out1), .out2(demultiplexer_1_out2),
    .out3(demultiplexer_1_out3), .in(WriteBack), .sel(Ra));
  Demultiplexer #(.select(2)) demultiplexer_2 (
    .out0(demultiplexer_2_out0), .out1(demultiplexer_2_out1), .out2(demultiplexer_2_out2),
    .out3(demultiplexer_2_out3), .in(WE), .sel(Ra));
  Register u_R0 (.D(demultiplexer_1_out0), .en(demultiplexer_2_out0), .clk(CLK), .Q(R0));  // open: clr
  Register u_R1 (.D(demultiplexer_1_out1), .en(demultiplexer_2_out1), .clk(CLK), .Q(R1));  // open: clr
  Register u_R2 (.D(demultiplexer_1_out2), .en(demultiplexer_2_out2), .clk(CLK), .Q(R2));  // open: clr
  Register u_R3 (.D(demultiplexer_1_out3), .en(demultiplexer_2_out3), .clk(CLK), .Q(R3));  // open: clr
  Multiplexer #(.select(2), .width(8)) multiplexer_1 (.in0(R0), .in1(R1), .in2(R2), .in3(R3), .out(Inf_a), .sel(Ra));
  Multiplexer #(.select(2), .width(8)) multiplexer_2 (.in0(R0), .in1(R1), .in2(R2), .in3(R3), .out(Inf_b), .sel(Rb));
endmodule

module intruct (
  input  [7:0] Inst,
  input  Type_I,
  output [3:0] opcode,
  output [1:0] R1,
  output [1:0] R2,
  output [3:0] imm
);

  Multiplexer #(.width(2)) multiplexer_1 (.in0(Inst[1:0]), .in1(2'b00), .out(R1), .sel(Type_I));

  assign imm = Inst[3:0];
  assign opcode = Inst[7:4];
  assign R2 = Inst[3:2];
endmodule

module ULA (
  input  [2:0] Ula_op,
  input  [7:0] Ra,
  input  [7:0] Rb,
  output zero,
  output [7:0] ULA_out
);

  wire adder_1_cout, or_4_out, subtractor_1_bout;
  wire [2:0] shift;
  wire [2:2] or_1_out;
  wire [7:0] adder_1_out, and_1_out, or_3_out, shifter_1_out, shifter_2_out, subtractor_1_out, xor_1_out;

  or or_1 (or_1_out[2], Rb[3], Rb[4], Rb[5], Rb[6], Rb[7]);
  assign shift = {3{or_1_out[2]}} | Rb[2:0];  // OR_Gate or_2, 3 bits wide
  Adder adder_1 (.a(Ra), .b(Rb), .out(adder_1_out), .cin(1'b0), .cout(adder_1_cout));
  // NoConnect on adder_1_cout
  Subtractor subtractor_1 (.a(Ra), .b(Rb), .out(subtractor_1_out), .bin(1'b0), .bout(subtractor_1_bout));
  // NoConnect on subtractor_1_bout
  Shifter shifter_1 (.in(Ra), .\dist (shift), .out(shifter_1_out));
  Shifter #(.shift("lr")) shifter_2 (.in(Ra), .\dist (shift), .out(shifter_2_out));
  assign and_1_out = Ra & Rb;  // AND_Gate and_1, 8 bits wide
  assign or_3_out = Ra | Rb;  // OR_Gate or_3, 8 bits wide
  assign xor_1_out = Ra ^ Rb;  // XOR_Gate xor_1, 8 bits wide
  Multiplexer #(.select(3), .width(8)) multiplexer_1 (
    .in0({8{1'b0}}), .in1(adder_1_out), .in2(subtractor_1_out), .in3(shifter_1_out), .in4(shifter_2_out),
    .in5(and_1_out), .in6(or_3_out), .in7(xor_1_out), .out(ULA_out), .sel(Ula_op));
  or or_4 (or_4_out, subtractor_1_out[0], subtractor_1_out[1], subtractor_1_out[2], subtractor_1_out[3], subtractor_1_out[4], subtractor_1_out[5], subtractor_1_out[6], subtractor_1_out[7]);
  not not_1 (zero, or_4_out);
endmodule

module Dual_port_RAM (
  input  [7:0] addr,
  input  [7:0] pc,
  input  [7:0] d,
  input  w,
  output [7:0] instr,
  output [7:0] data
);

  wire clock_1_out, or_1_out, undriven;
  wire [7:0] multiplexer_1_out;

  Clock clock_1 (.out(clock_1_out));
  or or_1 (or_1_out, w, clock_1_out);
  Multiplexer #(.width(8)) multiplexer_1 (.in0(addr), .in1(pc), .out(multiplexer_1_out), .sel(clock_1_out));
  RAM #(.asyncread("true")) ram_1 (
    .addr(multiplexer_1_out), .we(or_1_out), .oe(undriven), .clk(clock_1_out), .din(d), .dout(data));
  Register #(.trigger("falling")) pcbuf (.D(data), .en(1'b1), .clk(clock_1_out), .Q(instr));  // open: clr
endmodule
