// Digital circuit Banco de registradores.dig as structural Verilog
module Banco_de_registradores (
  input  [31:0] C,
  input  [3:0] S_A,
  input  [3:0] S_B,
  input  [3:0] S_C,
  input  CLK,
  input  W_En,
  output [31:0] A,
  output [31:0] B
);

  wire En_0, En_1, En_2, En_3, En_4, En_5, En_6, En_7, En_8, En_9, En_10, En_11, En_12, En_13, En_14, En_15;
  wire [31:0] demultiplexer_2_out_1, demultiplexer_2_out_2, demultiplexer_2_out_3, demultiplexer_2_out_4,
       demultiplexer_2_out_5, demultiplexer_2_out_6, demultiplexer_2_out_7, demultiplexer_2_out_8,
       demultiplexer_2_out_9, demultiplexer_2_out_10, demultiplexer_2_out_11, demultiplexer_2_out_12,
       demultiplexer_2_out_13, demultiplexer_2_out_14, demultiplexer_2_out_15, R_0, R_1, R_2, R_3, R_4, R_5,
       R_6, R_7, R_8, R_9, R_10, R_11, R_12, R_13, R_14, R_15;

  Demultiplexer #(.Selector_Bits(4)) demultiplexer_1 (
    .sel(S_C), .in(W_En), .out_0(En_0), .out_1(En_1), .out_2(En_2), .out_3(En_3), .out_4(En_4), .out_5(En_5),
    .out_6(En_6), .out_7(En_7), .out_8(En_8), .out_9(En_9), .out_10(En_10), .out_11(En_11), .out_12(En_12),
    .out_13(En_13), .out_14(En_14), .out_15(En_15));
  Demultiplexer #(.Selector_Bits(4), .Bits(32)) demultiplexer_2 (
    .sel(S_C), .in(C), .out_1(demultiplexer_2_out_1), .out_2(demultiplexer_2_out_2),
    .out_3(demultiplexer_2_out_3), .out_4(demultiplexer_2_out_4), .out_5(demultiplexer_2_out_5),
    .out_6(demultiplexer_2_out_6), .out_7(demultiplexer_2_out_7), .out_8(demultiplexer_2_out_8),
    .out_9(demultiplexer_2_out_9), .out_10(demultiplexer_2_out_10), .out_11(demultiplexer_2_out_11),
    .out_12(demultiplexer_2_out_12), .out_13(demultiplexer_2_out_13), .out_14(demultiplexer_2_out_14),
    .out_15(demultiplexer_2_out_15));  // open: out_0
  Registrador_32_bits registrador_32_bits_1 (.D({32{1'b0}}), .En(En_0), .CLK(CLK), .Q(R_0));
  Registrador_32_bits registrador_32_bits_2 (.D(demultiplexer_2_out_1), .En(En_1), .CLK(CLK), .Q(R_1));
  Registrador_32_bits registrador_32_bits_3 (.D(demultiplexer_2_out_2), .En(En_2), .CLK(CLK), .Q(R_2));
  Registrador_32_bits registrador_32_bits_4 (.D(demultiplexer_2_out_3), .En(En_3), .CLK(CLK), .Q(R_3));
  Registrador_32_bits registrador_32_bits_5 (.D(demultiplexer_2_out_4), .En(En_4), .CLK(CLK), .Q(R_4));
  Registrador_32_bits registrador_32_bits_6 (.D(demultiplexer_2_out_5), .En(En_5), .CLK(CLK), .Q(R_5));
  Registrador_32_bits registrador_32_bits_7 (.D(demultiplexer_2_out_6), .En(En_6), .CLK(CLK), .Q(R_6));
  Registrador_32_bits registrador_32_bits_8 (.D(demultiplexer_2_out_7), .En(En_7), .CLK(CLK), .Q(R_7));
  Registrador_32_bits registrador_32_bits_9 (.D(demultiplexer_2_out_8), .En(En_8), .CLK(CLK), .Q(R_8));
  Registrador_32_bits registrador_32_bits_10 (.D(demultiplexer_2_out_9), .En(En_9), .CLK(CLK), .Q(R_9));
  Registrador_32_bits registrador_32_bits_11 (.D(demultiplexer_2_out_10), .En(En_10), .CLK(CLK), .Q(R_10));
  Registrador_32_bits registrador_32_bits_12 (.D(demultiplexer_2_out_11), .En(En_11), .CLK(CLK), .Q(R_11));
  Registrador_32_bits registrador_32_bits_13 (.D(demultiplexer_2_out_12), .En(En_12), .CLK(CLK), .Q(R_12));
  Registrador_32_bits registrador_32_bits_14 (.D(demultiplexer_2_out_13), .En(En_13), .CLK(CLK), .Q(R_13));
  Registrador_32_bits registrador_32_bits_15 (.D(demultiplexer_2_out_14), .En(En_14), .CLK(CLK), .Q(R_14));
  Registrador_32_bits registrador_32_bits_16 (.D(demultiplexer_2_out_15), .En(En_15), .CLK(CLK), .Q(R_15));
  Multiplexer #(.Selector_Bits(4), .Bits(32)) multiplexer_1 (
    .sel(S_A), .in_0(R_0), .in_1(R_1), .in_2(R_2), .in_3(R_3), .in_4(R_4), .in_5(R_5), .in_6(R_6),
    .in_7(R_7), .in_8(R_8), .in_9(R_9), .in_10(R_10), .in_11(R_11), .in_12(R_12), .in_13(R_13), .in_14(R_14),
    .in_15(R_15), .out(A));
  Multiplexer #(.Selector_Bits(4), .Bits(32)) multiplexer_2 (
    .sel(S_B), .in_0(R_0), .in_1(R_1), .in_2(R_2), .in_3(R_3), .in_4(R_4), .in_5(R_5), .in_6(R_6),
    .in_7(R_7), .in_8(R_8), .in_9(R_9), .in_10(R_10), .in_11(R_11), .in_12(R_12), .in_13(R_13), .in_14(R_14),
    .in_15(R_15), .out(B));
endmodule
