// Digital circuit Extensor de zeros.dig as structural Verilog
module Extensor_de_zeros (
  input  [15:0] A,
  output [31:0] S
);

  // Pins of 1 and 16 bits meet at {S[31:17], 1'b0}
  // Pins of 1 and 32 bits meet at {S[31:17], 1'b0, A}

  assign S[16:0] = {1'b0, A};
endmodule
