// Digital circuit Instrução.dig as structural Verilog
module \Instrução  (
  input  [31:0] in,
  output [3:0] op,
  output [3:0] a,
  output [3:0] b,
  output [3:0] c,
  output [15:0] \const 
);


  assign a = in[27:24];
  assign b = in[23:20];
  assign c = in[19:16];
  assign \const  = in[15:0];
  assign op = in[31:28];
endmodule
