// Digital circuit Registrador 2 bits.dig as structural Verilog
module Registrador_2_bits (
  input  [1:0] entrada_2bits,
  input  Enabler,
  input  CLK,
  output Q0,
  output Q1
);

  wire d_ff_1_nq, multiplexer_1_out, multiplexer_2_out;

  Multiplexer multiplexer_1 (.sel(Enabler), .in_0(Q0), .in_1(entrada_2bits[0]), .out(multiplexer_1_out));
  Multiplexer multiplexer_2 (.sel(Enabler), .in_0(Q1), .in_1(entrada_2bits[1]), .out(multiplexer_2_out));
  D_FF d_ff_1 (.D(multiplexer_1_out), .C(CLK), .Q(Q0), .nQ(d_ff_1_nq));
  D_FF d_ff_2 (.D(multiplexer_2_out), .C(CLK), .Q(Q1), .nQ(d_ff_1_nq));
  // also tied to GND on the sheet: d_ff_1_nq
endmodule
