// Digital circuit Registrador 32 bits.dig as structural Verilog
module Registrador_32_bits (
  input  [31:0] D,
  input  En,
  input  CLK,
  output [31:0] Q
);

  wire multiplexer_1_out, multiplexer_2_out, multiplexer_3_out, multiplexer_4_out, multiplexer_5_out,
       multiplexer_6_out, multiplexer_7_out, multiplexer_8_out, multiplexer_9_out, multiplexer_10_out,
       multiplexer_11_out, multiplexer_12_out, multiplexer_13_out, multiplexer_14_out, multiplexer_15_out,
       multiplexer_16_out, multiplexer_17_out, multiplexer_18_out, multiplexer_19_out, multiplexer_20_out,
       multiplexer_21_out, multiplexer_22_out, multiplexer_23_out, multiplexer_24_out, multiplexer_25_out,
       multiplexer_26_out, multiplexer_27_out, multiplexer_28_out, multiplexer_29_out, multiplexer_30_out,
       multiplexer_31_out, multiplexer_32_out;

  Multiplexer multiplexer_1 (.sel(En), .in_0(Q[0]), .in_1(D[0]), .out(multiplexer_1_out));
  Multiplexer multiplexer_2 (.sel(En), .in_0(Q[1]), .in_1(D[1]), .out(multiplexer_2_out));
  Multiplexer multiplexer_3 (.sel(En), .in_0(Q[2]), .in_1(D[2]), .out(multiplexer_3_out));
  Multiplexer multiplexer_4 (.sel(En), .in_0(Q[3]), .in_1(D[3]), .out(multiplexer_4_out));
  Multiplexer multiplexer_5 (.sel(En), .in_0(Q[4]), .in_1(D[4]), .out(multiplexer_5_out));
  Multiplexer multiplexer_6 (.sel(En), .in_0(Q[5]), .in_1(D[5]), .out(multiplexer_6_out));
  Multiplexer multiplexer_7 (.sel(En), .in_0(Q[6]), .in_1(D[6]), .out(multiplexer_7_out));
  Multiplexer multiplexer_8 (.sel(En), .in_0(Q[7]), .in_1(D[7]), .out(multiplexer_8_out));
  Multiplexer multiplexer_9 (.sel(En), .in_0(Q[8]), .in_1(D[8]), .out(multiplexer_9_out));
  Multiplexer multiplexer_10 (.sel(En), .in_0(Q[9]), .in_1(D[9]), .out(multiplexer_10_out));
  Multiplexer multiplexer_11 (.sel(En), .in_0(Q[10]), .in_1(D[10]), .out(multiplexer_11_out));
  Multiplexer multiplexer_12 (.sel(En), .in_0(Q[11]), .in_1(D[11]), .out(multiplexer_12_out));
  Multiplexer multiplexer_13 (.sel(En), .in_0(Q[12]), .in_1(D[12]), .out(multiplexer_13_out));
  Multiplexer multiplexer_14 (.sel(En), .in_0(Q[13]), .in_1(D[13]), .out(multiplexer_14_out));
  Multiplexer multiplexer_15 (.sel(En), .in_0(Q[14]), .in_1(D[14]), .out(multiplexer_15_out));
  Multiplexer multiplexer_16 (.sel(En), .in_0(Q[15]), .in_1(D[15]), .out(multiplexer_16_out));
  Multiplexer multiplexer_17 (.sel(En), .in_0(Q[16]), .in_1(D[16]), .out(multiplexer_17_out));
  Multiplexer multiplexer_18 (.sel(En), .in_0(Q[17]), .in_1(D[17]), .out(multiplexer_18_out));
  Multiplexer multiplexer_19 (.sel(En), .in_0(Q[18]), .in_1(D[18]), .out(multiplexer_19_out));
  Multiplexer multiplexer_20 (.sel(En), .in_0(Q[19]), .in_1(D[19]), .out(multiplexer_20_out));
  Multiplexer multiplexer_21 (.sel(En), .in_0(Q[20]), .in_1(D[20]), .out(multiplexer_21_out));
  Multiplexer multiplexer_22 (.sel(En), .in_0(Q[21]), .in_1(D[21]), .out(multiplexer_22_out));
  Multiplexer multiplexer_23 (.sel(En), .in_0(Q[22]), .in_1(D[22]), .out(multiplexer_23_out));
  Multiplexer multiplexer_24 (.sel(En), .in_0(Q[23]), .in_1(D[23]), .out(multiplexer_24_out));
  Multiplexer multiplexer_25 (.sel(En), .in_0(Q[24]), .in_1(D[24]), .out(multiplexer_25_out));
  Multiplexer multiplexer_26 (.sel(En), .in_0(Q[25]), .in_1(D[25]), .out(multiplexer_26_out));
  Multiplexer multiplexer_27 (.sel(En), .in_0(Q[26]), .in_1(D[26]), .out(multiplexer_27_out));
  Multiplexer multiplexer_28 (.sel(En), .in_0(Q[27]), .in_1(D[27]), .out(multiplexer_28_out));
  Multiplexer multiplexer_29 (.sel(En), .in_0(Q[28]), .in_1(D[28]), .out(multiplexer_29_out));
  Multiplexer multiplexer_30 (.sel(En), .in_0(Q[29]), .in_1(D[29]), .out(multiplexer_30_out));
  Multiplexer multiplexer_31 (.sel(En), .in_0(Q[30]), .in_1(D[30]), .out(multiplexer_31_out));
  Multiplexer multiplexer_32 (.sel(En), .in_0(Q[31]), .in_1(D[31]), .out(multiplexer_32_out));
  D_FF d_ff_1 (.D(multiplexer_1_out), .C(CLK), .Q(Q[0]));  // open: nQ
  D_FF d_ff_2 (.D(multiplexer_2_out), .C(CLK), .Q(Q[1]));  // open: nQ
  D_FF d_ff_3 (.D(multiplexer_3_out), .C(CLK), .Q(Q[2]));  // open: nQ
  D_FF d_ff_4 (.D(multiplexer_4_out), .C(CLK), .Q(Q[3]));  // open: nQ
  D_FF d_ff_5 (.D(multiplexer_5_out), .C(CLK), .Q(Q[4]));  // open: nQ
  D_FF d_ff_6 (.D(multiplexer_6_out), .C(CLK), .Q(Q[5]));  // open: nQ
  D_FF d_ff_7 (.D(multiplexer_7_out), .C(CLK), .Q(Q[6]));  // open: nQ
  D_FF d_ff_8 (.D(multiplexer_8_out), .C(CLK), .Q(Q[7]));  // open: nQ
  D_FF d_ff_9 (.D(multiplexer_9_out), .C(CLK), .Q(Q[8]));  // open: nQ
  D_FF d_ff_10 (.D(multiplexer_10_out), .C(CLK), .Q(Q[9]));  // open: nQ
  D_FF d_ff_11 (.D(multiplexer_11_out), .C(CLK), .Q(Q[10]));  // open: nQ
  D_FF d_ff_12 (.D(multiplexer_12_out), .C(CLK), .Q(Q[11]));  // open: nQ
  D_FF d_ff_13 (.D(multiplexer_13_out), .C(CLK), .Q(Q[12]));  // open: nQ
  D_FF d_ff_14 (.D(multiplexer_14_out), .C(CLK), .Q(Q[13]));  // open: nQ
  D_FF d_ff_15 (.D(multiplexer_15_out), .C(CLK), .Q(Q[14]));  // open: nQ
  D_FF d_ff_16 (.D(multiplexer_16_out), .C(CLK), .Q(Q[15]));  // open: nQ
  D_FF d_ff_17 (.D(multiplexer_17_out), .C(CLK), .Q(Q[16]));  // open: nQ
  D_FF d_ff_18 (.D(multiplexer_18_out), .C(CLK), .Q(Q[17]));  // open: nQ
  D_FF d_ff_19 (.D(multiplexer_19_out), .C(CLK), .Q(Q[18]));  // open: nQ
  D_FF d_ff_20 (.D(multiplexer_20_out), .C(CLK), .Q(Q[19]));  // open: nQ
  D_FF d_ff_21 (.D(multiplexer_21_out), .C(CLK), .Q(Q[20]));  // open: nQ
  D_FF d_ff_22 (.D(multiplexer_22_out), .C(CLK), .Q(Q[21]));  // open: nQ
  D_FF d_ff_23 (.D(multiplexer_23_out), .C(CLK), .Q(Q[22]));  // open: nQ
  D_FF d_ff_24 (.D(multiplexer_24_out), .C(CLK), .Q(Q[23]));  // open: nQ
  D_FF d_ff_25 (.D(multiplexer_25_out), .C(CLK), .Q(Q[24]));  // open: nQ
  D_FF d_ff_26 (.D(multiplexer_26_out), .C(CLK), .Q(Q[25]));  // open: nQ
  D_FF d_ff_27 (.D(multiplexer_27_out), .C(CLK), .Q(Q[26]));  // open: nQ
  D_FF d_ff_28 (.D(multiplexer_28_out), .C(CLK), .Q(Q[27]));  // open: nQ
  D_FF d_ff_29 (.D(multiplexer_29_out), .C(CLK), .Q(Q[28]));  // open: nQ
  D_FF d_ff_30 (.D(multiplexer_30_out), .C(CLK), .Q(Q[29]));  // open: nQ
  D_FF d_ff_31 (.D(multiplexer_31_out), .C(CLK), .Q(Q[30]));  // open: nQ
  D_FF d_ff_32 (.D(multiplexer_32_out), .C(CLK), .Q(Q[31]));  // open: nQ
endmodule
