// Digital circuit Sinal de controle.dig as structural Verilog
module Sinal_de_controle (
  input  [8:0] in,
  output W_en,
  output Branch,
  output ULA_imm,
  output [2:0] ULA_op,
  output Display,
  output Halt,
  output Jump
);


  assign Branch = in[1];
  assign Display = in[6];
  assign Halt = in[7];
  assign Jump = in[8];
  assign ULA_imm = in[2];
  assign ULA_op = in[5:3];
  assign W_en = in[0];
endmodule
