// Digital circuit Somador 1 bit.dig as structural Verilog
module Somador_1_bit (
  input  A,
  input  B,
  input  C_i,
  output S,
  output C_o
);

  wire and_1_out, and_2_out, and_3_out;

  and and_1 (and_1_out, A, B);
  and and_2 (and_2_out, A, C_i);
  and and_3 (and_3_out, B, C_i);
  xor xor_1 (S, A, B, C_i);
  or or_1 (C_o, and_1_out, and_2_out, and_3_out);
endmodule
