// Digital circuit Somador 2 bits.dig as structural Verilog
module Somador_2_bits (
  input  [1:0] A,
  input  [1:0] B,
  input  C_i,
  output [1:0] S,
  output C_o
);

  wire somador_1_bit_1_c_o;

  Somador_1_bit somador_1_bit_1 (.A(A[0]), .B(B[0]), .C_i(C_i), .S(S[0]), .C_o(somador_1_bit_1_c_o));
  Somador_1_bit somador_1_bit_2 (.A(A[1]), .B(B[1]), .C_i(somador_1_bit_1_c_o), .S(S[1]), .C_o(C_o));
endmodule
