// Digital circuit Somador 32 bits.dig as structural Verilog
module Somador_32_bits (
  input  [31:0] A,
  input  [31:0] B,
  input  C_i,
  output [31:0] S,
  output C_o
);

  wire somador_8_bits_1_c_o, somador_8_bits_2_c_o, somador_8_bits_3_c_o;

  Somador_8_bits somador_8_bits_1 (.A(A[7:0]), .B(B[7:0]), .C_i(C_i), .S(S[7:0]), .C_o(somador_8_bits_1_c_o));
  Somador_8_bits somador_8_bits_2 (
    .A(A[15:8]), .B(B[15:8]), .C_i(somador_8_bits_1_c_o), .S(S[15:8]), .C_o(somador_8_bits_2_c_o));
  Somador_8_bits somador_8_bits_3 (
    .A(A[23:16]), .B(B[23:16]), .C_i(somador_8_bits_2_c_o), .S(S[23:16]), .C_o(somador_8_bits_3_c_o));
  Somador_8_bits somador_8_bits_4 (.A(A[31:24]), .B(B[31:24]), .C_i(somador_8_bits_3_c_o), .S(S[31:24]), .C_o(C_o));
endmodule
