// Digital circuit Somador 4 bits.dig as structural Verilog
module Somador_4_bits (
  input  [3:0] A,
  input  [3:0] B,
  input  C_i,
  output [3:0] S,
  output C_o
);

  wire somador_2_bits_1_c_o;

  Somador_2_bits somador_2_bits_1 (.A(A[1:0]), .B(B[1:0]), .C_i(C_i), .S(S[3:2]), .C_o(somador_2_bits_1_c_o));
  // Somador_2_bits somador_2_bits_2: pin names not known; wires that end beside it: A[3:2], B[3:2], somador_2_bits_1_c_o, C_o, S[1:0]
endmodule
