// Digital circuit Somador 8 bits.dig as structural Verilog
module Somador_8_bits (
  input  [7:0] A,
  input  [7:0] B,
  input  C_i,
  output [7:0] S,
  output C_o
);

  wire somador_2_bits_1_c_o, somador_2_bits_2_c_o, somador_2_bits_3_c_o;

  Somador_2_bits somador_2_bits_1 (.A(A[1:0]), .B(B[1:0]), .C_i(C_i), .S(S[1:0]), .C_o(somador_2_bits_1_c_o));
  Somador_2_bits somador_2_bits_2 (
    .A(A[3:2]), .B(B[3:2]), .C_i(somador_2_bits_1_c_o), .S(S[3:2]), .C_o(somador_2_bits_2_c_o));
  Somador_2_bits somador_2_bits_3 (
    .A(A[5:4]), .B(B[5:4]), .C_i(somador_2_bits_2_c_o), .S(S[5:4]), .C_o(somador_2_bits_3_c_o));
  Somador_2_bits somador_2_bits_4 (.A(A[7:6]), .B(B[7:6]), .C_i(somador_2_bits_3_c_o), .S(S[7:6]), .C_o(C_o));
endmodule
