// Digital circuit Subtrator 32 bits.dig as structural Verilog
module Subtrator_32_bits (
  input  [31:0] A,
  input  [31:0] B,
  output C_out,
  output [31:0] S
);

  wire [31:0] not_1_out;

  assign not_1_out = ~B;  // Not not_1, 32 bits wide
  Somador_32_bits somador_32_bits_1 (.A(A), .B(not_1_out), .C_i(1'b1), .S(S), .C_o(C_out));
endmodule
