// Digital circuit ULA.dig as structural Verilog
module ULA (
  input  [31:0] A,
  input  [31:0] B,
  input  [2:0] Sele,
  output [31:0] S,
  output zero
);

  wire [31:0] and_1_out, or_1_out, shifter_32_bits_1_s, somador_32_bits_1_s, subtrator_32_bits_1_s, xor_1_out;
  wire [63:0] mul_1_mul;

  Somador_32_bits somador_32_bits_1 (.A(A), .B(B), .C_i(1'b0), .S(somador_32_bits_1_s));  // open: C_o
  Subtrator_32_bits subtrator_32_bits_1 (.A(A), .B(B), .S(subtrator_32_bits_1_s));  // open: C_out
  Mul #(.Bits(32)) mul_1 (.a(A), .b(B), .mul(mul_1_mul));
  assign and_1_out = A & B;  // And and_1, 32 bits wide
  assign or_1_out = A | B;  // Or or_1, 32 bits wide
  assign xor_1_out = A ^ B;  // XOr xor_1, 32 bits wide
  shifter_32_bits shifter_32_bits_1 (.A(A), .B(B), .S(shifter_32_bits_1_s));
  Multiplexer #(.Selector_Bits(3), .Bits(32)) multiplexer_1 (
    .sel(Sele), .in_0(somador_32_bits_1_s), .in_1(subtrator_32_bits_1_s), .in_2(mul_1_mul[31:0]),
    .in_3(and_1_out), .in_4(or_1_out), .in_5(xor_1_out), .in_6(shifter_32_bits_1_s), .in_7({32{1'b0}}),
    .out(S));
  nor nor_1 (zero, S[31], S[30], S[29], S[28], S[27], S[26], S[25], S[24], S[23], S[22], S[21], S[20], S[19], S[18], S[17], S[16], S[15], S[14], S[13], S[12], S[11], S[10], S[9], S[8], S[7], S[6], S[5], S[4], S[3], S[2], S[1], S[0]);
endmodule
