// Digital circuit shifter 32 bits.dig as structural Verilog
module shifter_32_bits (
  input  [31:0] A,
  input  [31:0] B,
  output [31:0] S
);

  wire or_1_out, or_2_out, or_3_out, or_4_out, or_5_out, or_6_out, or_7_out, or_8_out, or_9_out, S_0, S_1,
       S_2, S_3, S_4, S_5, S_6, S_7, S_8, S_9, S_10, S_11, S_12, S_13, S_14, S_15, S_16, S_17, S_18, S_19,
       S_20, S_21, S_22, S_23, S_24, S_25, S_26, S_27, S_28, S_29, S_30, S_31;

  Multiplexer #(.Selector_Bits(5)) multiplexer_1 (
    .sel(B[4:0]), .in_0(A[0]), .in_1(1'b0), .in_2(1'b0), .in_3(1'b0), .in_4(1'b0), .in_5(1'b0), .in_6(1'b0),
    .in_7(1'b0), .in_8(1'b0), .in_9(1'b0), .in_10(1'b0), .in_11(1'b0), .in_12(1'b0), .in_13(1'b0),
    .in_14(1'b0), .in_15(1'b0), .in_16(1'b0), .in_17(1'b0), .in_18(1'b0), .in_19(1'b0), .in_20(1'b0),
    .in_21(1'b0), .in_22(1'b0), .in_23(1'b0), .in_24(1'b0), .in_25(1'b0), .in_26(1'b0), .in_27(1'b0),
    .in_28(1'b0), .in_29(1'b0), .in_30(1'b0), .in_31(1'b0), .out(S_0));
  Multiplexer #(.Selector_Bits(5)) multiplexer_2 (
    .sel(B[4:0]), .in_0(A[1]), .in_1(A[0]), .in_2(1'b0), .in_3(1'b0), .in_4(1'b0), .in_5(1'b0), .in_6(1'b0),
    .in_7(1'b0), .in_8(1'b0), .in_9(1'b0), .in_10(1'b0), .in_11(1'b0), .in_12(1'b0), .in_13(1'b0),
    .in_14(1'b0), .in_15(1'b0), .in_16(1'b0), .in_17(1'b0), .in_18(1'b0), .in_19(1'b0), .in_20(1'b0),
    .in_21(1'b0), .in_22(1'b0), .in_23(1'b0), .in_24(1'b0), .in_25(1'b0), .in_26(1'b0), .in_27(1'b0),
    .in_28(1'b0), .in_29(1'b0), .in_30(1'b0), .in_31(1'b0), .out(S_1));
  Multiplexer #(.Selector_Bits(5)) multiplexer_3 (
    .sel(B[4:0]), .in_0(A[2]), .in_1(A[1]), .in_2(A[0]), .in_3(1'b0), .in_4(1'b0), .in_5(1'b0), .in_6(1'b0),
    .in_7(1'b0), .in_8(1'b0), .in_9(1'b0), .in_10(1'b0), .in_11(1'b0), .in_12(1'b0), .in_13(1'b0),
    .in_14(1'b0), .in_15(1'b0), .in_16(1'b0), .in_17(1'b0), .in_18(1'b0), .in_19(1'b0), .in_20(1'b0),
    .in_21(1'b0), .in_22(1'b0), .in_23(1'b0), .in_24(1'b0), .in_25(1'b0), .in_26(1'b0), .in_27(1'b0),
    .in_28(1'b0), .in_29(1'b0), .in_30(1'b0), .in_31(1'b0), .out(S_2));
  Multiplexer #(.Selector_Bits(5)) multiplexer_4 (
    .sel(B[4:0]), .in_0(A[3]), .in_1(A[2]), .in_2(A[1]), .in_3(A[0]), .in_4(1'b0), .in_5(1'b0), .in_6(1'b0),
    .in_7(1'b0), .in_8(1'b0), .in_9(1'b0), .in_10(1'b0), .in_11(1'b0), .in_12(1'b0), .in_13(1'b0),
    .in_14(1'b0), .in_15(1'b0), .in_16(1'b0), .in_17(1'b0), .in_18(1'b0), .in_19(1'b0), .in_20(1'b0),
    .in_21(1'b0), .in_22(1'b0), .in_23(1'b0), .in_24(1'b0), .in_25(1'b0), .in_26(1'b0), .in_27(1'b0),
    .in_28(1'b0), .in_29(1'b0), .in_30(1'b0), .in_31(1'b0), .out(S_3));
  Multiplexer #(.Selector_Bits(5)) multiplexer_5 (
    .sel(B[4:0]), .in_0(A[4]), .in_1(A[3]), .in_2(A[2]), .in_3(A[1]), .in_4(A[0]), .in_5(1'b0), .in_6(1'b0),
    .in_7(1'b0), .in_8(1'b0), .in_9(1'b0), .in_10(1'b0), .in_11(1'b0), .in_12(1'b0), .in_13(1'b0),
    .in_14(1'b0), .in_15(1'b0), .in_16(1'b0), .in_17(1'b0), .in_18(1'b0), .in_19(1'b0), .in_20(1'b0),
    .in_21(1'b0), .in_22(1'b0), .in_23(1'b0), .in_24(1'b0), .in_25(1'b0), .in_26(1'b0), .in_27(1'b0),
    .in_28(1'b0), .in_29(1'b0), .in_30(1'b0), .in_31(1'b0), .out(S_4));
  Multiplexer #(.Selector_Bits(5)) multiplexer_6 (
    .sel(B[4:0]), .in_0(A[5]), .in_1(A[4]), .in_2(A[3]), .in_3(A[2]), .in_4(A[1]), .in_5(A[0]), .in_6(1'b0),
    .in_7(1'b0), .in_8(1'b0), .in_9(1'b0), .in_10(1'b0), .in_11(1'b0), .in_12(1'b0), .in_13(1'b0),
    .in_14(1'b0), .in_15(1'b0), .in_16(1'b0), .in_17(1'b0), .in_18(1'b0), .in_19(1'b0), .in_20(1'b0),
    .in_21(1'b0), .in_22(1'b0), .in_23(1'b0), .in_24(1'b0), .in_25(1'b0), .in_26(1'b0), .in_27(1'b0),
    .in_28(1'b0), .in_29(1'b0), .in_30(1'b0), .in_31(1'b0), .out(S_5));
  Multiplexer #(.Selector_Bits(5)) multiplexer_7 (
    .sel(B[4:0]), .in_0(A[6]), .in_1(A[5]), .in_2(A[4]), .in_3(A[3]), .in_4(A[2]), .in_5(A[1]), .in_6(A[0]),
    .in_7(1'b0), .in_8(1'b0), .in_9(1'b0), .in_10(1'b0), .in_11(1'b0), .in_12(1'b0), .in_13(1'b0),
    .in_14(1'b0), .in_15(1'b0), .in_16(1'b0), .in_17(1'b0), .in_18(1'b0), .in_19(1'b0), .in_20(1'b0),
    .in_21(1'b0), .in_22(1'b0), .in_23(1'b0), .in_24(1'b0), .in_25(1'b0), .in_26(1'b0), .in_27(1'b0),
    .in_28(1'b0), .in_29(1'b0), .in_30(1'b0), .in_31(1'b0), .out(S_6));
  Multiplexer #(.Selector_Bits(5)) multiplexer_8 (
    .sel(B[4:0]), .in_0(A[7]), .in_1(A[6]), .in_2(A[5]), .in_3(A[4]), .in_4(A[3]), .in_5(A[2]), .in_6(A[1]),
    .in_7(A[0]), .in_8(1'b0), .in_9(1'b0), .in_10(1'b0), .in_11(1'b0), .in_12(1'b0), .in_13(1'b0),
    .in_14(1'b0), .in_15(1'b0), .in_16(1'b0), .in_17(1'b0), .in_18(1'b0), .in_19(1'b0), .in_20(1'b0),
    .in_21(1'b0), .in_22(1'b0), .in_23(1'b0), .in_24(1'b0), .in_25(1'b0), .in_26(1'b0), .in_27(1'b0),
    .in_28(1'b0), .in_29(1'b0), .in_30(1'b0), .in_31(1'b0), .out(S_7));
  Multiplexer #(.Selector_Bits(5)) multiplexer_9 (
    .sel(B[4:0]), .in_0(A[8]), .in_1(A[7]), .in_2(A[6]), .in_3(A[5]), .in_4(A[4]), .in_5(A[3]), .in_6(A[2]),
    .in_7(A[1]), .in_8(A[0]), .in_9(1'b0), .in_10(1'b0), .in_11(1'b0), .in_12(1'b0), .in_13(1'b0),
    .in_14(1'b0), .in_15(1'b0), .in_16(1'b0), .in_17(1'b0), .in_18(1'b0), .in_19(1'b0), .in_20(1'b0),
    .in_21(1'b0), .in_22(1'b0), .in_23(1'b0), .in_24(1'b0), .in_25(1'b0), .in_26(1'b0), .in_27(1'b0),
    .in_28(1'b0), .in_29(1'b0), .in_30(1'b0), .in_31(1'b0), .out(S_8));
  Multiplexer #(.Selector_Bits(5)) multiplexer_10 (
    .sel(B[4:0]), .in_0(A[9]), .in_1(A[8]), .in_2(A[7]), .in_3(A[6]), .in_4(A[5]), .in_5(A[4]), .in_6(A[3]),
    .in_7(A[2]), .in_8(A[1]), .in_9(A[0]), .in_10(1'b0), .in_11(1'b0), .in_12(1'b0), .in_13(1'b0),
    .in_14(1'b0), .in_15(1'b0), .in_16(1'b0), .in_17(1'b0), .in_18(1'b0), .in_19(1'b0), .in_20(1'b0),
    .in_21(1'b0), .in_22(1'b0), .in_23(1'b0), .in_24(1'b0), .in_25(1'b0), .in_26(1'b0), .in_27(1'b0),
    .in_28(1'b0), .in_29(1'b0), .in_30(1'b0), .in_31(1'b0), .out(S_9));
  Multiplexer #(.Selector_Bits(5)) multiplexer_11 (
    .sel(B[4:0]), .in_0(A[10]), .in_1(A[9]), .in_2(A[8]), .in_3(A[7]), .in_4(A[6]), .in_5(A[5]), .in_6(A[4]),
    .in_7(A[3]), .in_8(A[2]), .in_9(A[1]), .in_10(A[0]), .in_11(1'b0), .in_12(1'b0), .in_13(1'b0),
    .in_14(1'b0), .in_15(1'b0), .in_16(1'b0), .in_17(1'b0), .in_18(1'b0), .in_19(1'b0), .in_20(1'b0),
    .in_21(1'b0), .in_22(1'b0), .in_23(1'b0), .in_24(1'b0), .in_25(1'b0), .in_26(1'b0), .in_27(1'b0),
    .in_28(1'b0), .in_29(1'b0), .in_30(1'b0), .in_31(1'b0), .out(S_10));
  Multiplexer #(.Selector_Bits(5)) multiplexer_12 (
    .sel(B[4:0]), .in_0(A[11]), .in_1(A[10]), .in_2(A[9]), .in_3(A[8]), .in_4(A[7]), .in_5(A[6]),
    .in_6(A[5]), .in_7(A[4]), .in_8(A[3]), .in_9(A[2]), .in_10(A[1]), .in_11(A[0]), .in_12(1'b0),
    .in_13(1'b0), .in_14(1'b0), .in_15(1'b0), .in_16(1'b0), .in_17(1'b0), .in_18(1'b0), .in_19(1'b0),
    .in_20(1'b0), .in_21(1'b0), .in_22(1'b0), .in_23(1'b0), .in_24(1'b0), .in_25(1'b0), .in_26(1'b0),
    .in_27(1'b0), .in_28(1'b0), .in_29(1'b0), .in_30(1'b0), .in_31(1'b0), .out(S_11));
  Multiplexer #(.Selector_Bits(5)) multiplexer_13 (
    .sel(B[4:0]), .in_0(A[12]), .in_1(A[11]), .in_2(A[10]), .in_3(A[9]), .in_4(A[8]), .in_5(A[7]),
    .in_6(A[6]), .in_7(A[5]), .in_8(A[4]), .in_9(A[3]), .in_10(A[2]), .in_11(A[1]), .in_12(A[0]),
    .in_13(1'b0), .in_14(1'b0), .in_15(1'b0), .in_16(1'b0), .in_17(1'b0), .in_18(1'b0), .in_19(1'b0),
    .in_20(1'b0), .in_21(1'b0), .in_22(1'b0), .in_23(1'b0), .in_24(1'b0), .in_25(1'b0), .in_26(1'b0),
    .in_27(1'b0), .in_28(1'b0), .in_29(1'b0), .in_30(1'b0), .in_31(1'b0), .out(S_12));
  or or_1 (or_1_out, B[5], B[6], B[7], B[8]);
  or or_2 (or_2_out, B[9], B[10], B[11], B[12]);
  or or_3 (or_3_out, B[13], B[14], B[15], B[16]);
  or or_4 (or_4_out, B[17], B[18], B[19], B[20]);
  or or_5 (or_5_out, B[21], B[22], B[23], B[24]);
  or or_6 (or_6_out, B[25], B[26], B[27], B[28]);
  or or_7 (or_7_out, B[29], B[30], B[31]);
  Multiplexer #(.Selector_Bits(5)) multiplexer_14 (
    .sel(B[4:0]), .in_0(A[13]), .in_1(A[12]), .in_2(A[11]), .in_3(A[10]), .in_4(A[9]), .in_5(A[8]),
    .in_6(A[7]), .in_7(A[6]), .in_8(A[5]), .in_9(A[4]), .in_10(A[3]), .in_11(A[2]), .in_12(A[1]),
    .in_13(A[0]), .in_14(1'b0), .in_15(1'b0), .in_16(1'b0), .in_17(1'b0), .in_18(1'b0), .in_19(1'b0),
    .in_20(1'b0), .in_21(1'b0), .in_22(1'b0), .in_23(1'b0), .in_24(1'b0), .in_25(1'b0), .in_26(1'b0),
    .in_27(1'b0), .in_28(1'b0), .in_29(1'b0), .in_30(1'b0), .in_31(1'b0), .out(S_13));
  or or_8 (or_8_out, or_1_out, or_2_out, or_3_out, or_4_out);
  or or_9 (or_9_out, or_8_out, or_5_out, or_6_out, or_7_out);
  Multiplexer #(.Selector_Bits(5)) multiplexer_15 (
    .sel(B[4:0]), .in_0(A[14]), .in_1(A[13]), .in_2(A[12]), .in_3(A[11]), .in_4(A[10]), .in_5(A[9]),
    .in_6(A[8]), .in_7(A[7]), .in_8(A[6]), .in_9(A[5]), .in_10(A[4]), .in_11(A[3]), .in_12(A[2]),
    .in_13(A[1]), .in_14(A[0]), .in_15(1'b0), .in_16(1'b0), .in_17(1'b0), .in_18(1'b0), .in_19(1'b0),
    .in_20(1'b0), .in_21(1'b0), .in_22(1'b0), .in_23(1'b0), .in_24(1'b0), .in_25(1'b0), .in_26(1'b0),
    .in_27(1'b0), .in_28(1'b0), .in_29(1'b0), .in_30(1'b0), .in_31(1'b0), .out(S_14));
  Multiplexer #(.Bits(32)) multiplexer_16 (
    .sel(or_9_out),
    .in_0({S_31, S_30, S_29, S_28, S_27, S_26, S_25, S_24, S_23, S_22, S_21, S_20, S_19, S_18, S_17, S_16, S_15, S_14, S_13, S_12, S_11, S_10, S_9, S_8, S_7, S_6, S_5, S_4, S_3, S_2, S_1, S_0}),
    .in_1({32{1'b0}}), .out(S));
  Multiplexer #(.Selector_Bits(5)) multiplexer_17 (
    .sel(B[4:0]), .in_0(A[15]), .in_1(A[14]), .in_2(A[13]), .in_3(A[12]), .in_4(A[11]), .in_5(A[10]),
    .in_6(A[9]), .in_7(A[8]), .in_8(A[7]), .in_9(A[6]), .in_10(A[5]), .in_11(A[4]), .in_12(A[3]),
    .in_13(A[2]), .in_14(A[1]), .in_15(A[0]), .in_16(1'b0), .in_17(1'b0), .in_18(1'b0), .in_19(1'b0),
    .in_20(1'b0), .in_21(1'b0), .in_22(1'b0), .in_23(1'b0), .in_24(1'b0), .in_25(1'b0), .in_26(1'b0),
    .in_27(1'b0), .in_28(1'b0), .in_29(1'b0), .in_30(1'b0), .in_31(1'b0), .out(S_15));
  Multiplexer #(.Selector_Bits(5)) multiplexer_18 (
    .sel(B[4:0]), .in_0(A[16]), .in_1(A[15]), .in_2(A[14]), .in_3(A[13]), .in_4(A[12]), .in_5(A[11]),
    .in_6(A[10]), .in_7(A[9]), .in_8(A[8]), .in_9(A[7]), .in_10(A[6]), .in_11(A[5]), .in_12(A[4]),
    .in_13(A[3]), .in_14(A[2]), .in_15(A[1]), .in_16(A[0]), .in_17(1'b0), .in_18(1'b0), .in_19(1'b0),
    .in_20(1'b0), .in_21(1'b0), .in_22(1'b0), .in_23(1'b0), .in_24(1'b0), .in_25(1'b0), .in_26(1'b0),
    .in_27(1'b0), .in_28(1'b0), .in_29(1'b0), .in_30(1'b0), .in_31(1'b0), .out(S_16));
  Multiplexer #(.Selector_Bits(5)) multiplexer_19 (
    .sel(B[4:0]), .in_0(A[17]), .in_1(A[16]), .in_2(A[15]), .in_3(A[14]), .in_4(A[13]), .in_5(A[12]),
    .in_6(A[11]), .in_7(A[10]), .in_8(A[9]), .in_9(A[8]), .in_10(A[7]), .in_11(A[6]), .in_12(A[5]),
    .in_13(A[4]), .in_14(A[3]), .in_15(A[2]), .in_16(A[1]), .in_17(A[0]), .in_18(1'b0), .in_19(1'b0),
    .in_20(1'b0), .in_21(1'b0), .in_22(1'b0), .in_23(1'b0), .in_24(1'b0), .in_25(1'b0), .in_26(1'b0),
    .in_27(1'b0), .in_28(1'b0), .in_29(1'b0), .in_30(1'b0), .in_31(1'b0), .out(S_17));
  Multiplexer #(.Selector_Bits(5)) multiplexer_20 (
    .sel(B[4:0]), .in_0(A[18]), .in_1(A[17]), .in_2(A[16]), .in_3(A[15]), .in_4(A[14]), .in_5(A[13]),
    .in_6(A[12]), .in_7(A[11]), .in_8(A[10]), .in_9(A[9]), .in_10(A[8]), .in_11(A[7]), .in_12(A[6]),
    .in_13(A[5]), .in_14(A[4]), .in_15(A[3]), .in_16(A[2]), .in_17(A[1]), .in_18(A[0]), .in_19(1'b0),
    .in_20(1'b0), .in_21(1'b0), .in_22(1'b0), .in_23(1'b0), .in_24(1'b0), .in_25(1'b0), .in_26(1'b0),
    .in_27(1'b0), .in_28(1'b0), .in_29(1'b0), .in_30(1'b0), .in_31(1'b0), .out(S_18));
  Multiplexer #(.Selector_Bits(5)) multiplexer_21 (
    .sel(B[4:0]), .in_0(A[19]), .in_1(A[18]), .in_2(A[17]), .in_3(A[16]), .in_4(A[15]), .in_5(A[14]),
    .in_6(A[13]), .in_7(A[12]), .in_8(A[11]), .in_9(A[10]), .in_10(A[9]), .in_11(A[8]), .in_12(A[7]),
    .in_13(A[6]), .in_14(A[5]), .in_15(A[4]), .in_16(A[3]), .in_17(A[2]), .in_18(A[1]), .in_19(A[0]),
    .in_20(1'b0), .in_21(1'b0), .in_22(1'b0), .in_23(1'b0), .in_24(1'b0), .in_25(1'b0), .in_26(1'b0),
    .in_27(1'b0), .in_28(1'b0), .in_29(1'b0), .in_30(1'b0), .in_31(1'b0), .out(S_19));
  Multiplexer #(.Selector_Bits(5)) multiplexer_22 (
    .sel(B[4:0]), .in_0(A[20]), .in_1(A[19]), .in_2(A[18]), .in_3(A[17]), .in_4(A[16]), .in_5(A[15]),
    .in_6(A[14]), .in_7(A[13]), .in_8(A[12]), .in_9(A[11]), .in_10(A[10]), .in_11(A[9]), .in_12(A[8]),
    .in_13(A[7]), .in_14(A[6]), .in_15(A[5]), .in_16(A[4]), .in_17(A[3]), .in_18(A[2]), .in_19(A[1]),
    .in_20(A[0]), .in_21(1'b0), .in_22(1'b0), .in_23(1'b0), .in_24(1'b0), .in_25(1'b0), .in_26(1'b0),
    .in_27(1'b0), .in_28(1'b0), .in_29(1'b0), .in_30(1'b0), .in_31(1'b0), .out(S_20));
  Multiplexer #(.Selector_Bits(5)) multiplexer_23 (
    .sel(B[4:0]), .in_0(A[21]), .in_1(A[20]), .in_2(A[19]), .in_3(A[18]), .in_4(A[17]), .in_5(A[16]),
    .in_6(A[15]), .in_7(A[14]), .in_8(A[13]), .in_9(A[12]), .in_10(A[11]), .in_11(A[10]), .in_12(A[9]),
    .in_13(A[8]), .in_14(A[7]), .in_15(A[6]), .in_16(A[5]), .in_17(A[4]), .in_18(A[3]), .in_19(A[2]),
    .in_20(A[1]), .in_21(A[0]), .in_22(1'b0), .in_23(1'b0), .in_24(1'b0), .in_25(1'b0), .in_26(1'b0),
    .in_27(1'b0), .in_28(1'b0), .in_29(1'b0), .in_30(1'b0), .in_31(1'b0), .out(S_21));
  Multiplexer #(.Selector_Bits(5)) multiplexer_24 (
    .sel(B[4:0]), .in_0(A[22]), .in_1(A[21]), .in_2(A[20]), .in_3(A[19]), .in_4(A[18]), .in_5(A[17]),
    .in_6(A[16]), .in_7(A[15]), .in_8(A[14]), .in_9(A[13]), .in_10(A[12]), .in_11(A[11]), .in_12(A[10]),
    .in_13(A[9]), .in_14(A[8]), .in_15(A[7]), .in_16(A[6]), .in_17(A[5]), .in_18(A[4]), .in_19(A[3]),
    .in_20(A[2]), .in_21(A[1]), .in_22(A[0]), .in_23(1'b0), .in_24(1'b0), .in_25(1'b0), .in_26(1'b0),
    .in_27(1'b0), .in_28(1'b0), .in_29(1'b0), .in_30(1'b0), .in_31(1'b0), .out(S_22));
  Multiplexer #(.Selector_Bits(5)) multiplexer_25 (
    .sel(B[4:0]), .in_0(A[23]), .in_1(A[22]), .in_2(A[21]), .in_3(A[20]), .in_4(A[19]), .in_5(A[18]),
    .in_6(A[17]), .in_7(A[16]), .in_8(A[15]), .in_9(A[14]), .in_10(A[13]), .in_11(A[12]), .in_12(A[11]),
    .in_13(A[10]), .in_14(A[9]), .in_15(A[8]), .in_16(A[7]), .in_17(A[6]), .in_18(A[5]), .in_19(A[4]),
    .in_20(A[3]), .in_21(A[2]), .in_22(A[1]), .in_23(A[0]), .in_24(1'b0), .in_25(1'b0), .in_26(1'b0),
    .in_27(1'b0), .in_28(1'b0), .in_29(1'b0), .in_30(1'b0), .in_31(1'b0), .out(S_23));
  Multiplexer #(.Selector_Bits(5)) multiplexer_26 (
    .sel(B[4:0]), .in_0(A[24]), .in_1(A[23]), .in_2(A[22]), .in_3(A[21]), .in_4(A[20]), .in_5(A[19]),
    .in_6(A[18]), .in_7(A[17]), .in_8(A[16]), .in_9(A[15]), .in_10(A[14]), .in_11(A[13]), .in_12(A[12]),
    .in_13(A[11]), .in_14(A[10]), .in_15(A[9]), .in_16(A[8]), .in_17(A[7]), .in_18(A[6]), .in_19(A[5]),
    .in_20(A[4]), .in_21(A[3]), .in_22(A[2]), .in_23(A[1]), .in_24(A[0]), .in_25(1'b0), .in_26(1'b0),
    .in_27(1'b0), .in_28(1'b0), .in_29(1'b0), .in_30(1'b0), .in_31(1'b0), .out(S_24));
  Multiplexer #(.Selector_Bits(5)) multiplexer_27 (
    .sel(B[4:0]), .in_0(A[25]), .in_1(A[24]), .in_2(A[23]), .in_3(A[22]), .in_4(A[21]), .in_5(A[20]),
    .in_6(A[19]), .in_7(A[18]), .in_8(A[17]), .in_9(A[16]), .in_10(A[15]), .in_11(A[14]), .in_12(A[13]),
    .in_13(A[12]), .in_14(A[11]), .in_15(A[10]), .in_16(A[9]), .in_17(A[8]), .in_18(A[7]), .in_19(A[6]),
    .in_20(A[5]), .in_21(A[4]), .in_22(A[3]), .in_23(A[2]), .in_24(A[1]), .in_25(A[0]), .in_26(1'b0),
    .in_27(1'b0), .in_28(1'b0), .in_29(1'b0), .in_30(1'b0), .in_31(1'b0), .out(S_25));
  Multiplexer #(.Selector_Bits(5)) multiplexer_28 (
    .sel(B[4:0]), .in_0(A[26]), .in_1(A[25]), .in_2(A[24]), .in_3(A[23]), .in_4(A[22]), .in_5(A[21]),
    .in_6(A[20]), .in_7(A[19]), .in_8(A[18]), .in_9(A[17]), .in_10(A[16]), .in_11(A[15]), .in_12(A[14]),
    .in_13(A[13]), .in_14(A[12]), .in_15(A[11]), .in_16(A[10]), .in_17(A[9]), .in_18(A[8]), .in_19(A[7]),
    .in_20(A[6]), .in_21(A[5]), .in_22(A[4]), .in_23(A[3]), .in_24(A[2]), .in_25(A[1]), .in_26(A[0]),
    .in_27(1'b0), .in_28(1'b0), .in_29(1'b0), .in_30(1'b0), .in_31(1'b0), .out(S_26));
  Multiplexer #(.Selector_Bits(5)) multiplexer_29 (
    .sel(B[4:0]), .in_0(A[27]), .in_1(A[26]), .in_2(A[25]), .in_3(A[24]), .in_4(A[23]), .in_5(A[22]),
    .in_6(A[21]), .in_7(A[20]), .in_8(A[19]), .in_9(A[18]), .in_10(A[17]), .in_11(A[16]), .in_12(A[15]),
    .in_13(A[14]), .in_14(A[13]), .in_15(A[12]), .in_16(A[11]), .in_17(A[10]), .in_18(A[9]), .in_19(A[8]),
    .in_20(A[7]), .in_21(A[6]), .in_22(A[5]), .in_23(A[4]), .in_24(A[3]), .in_25(A[2]), .in_26(A[1]),
    .in_27(A[0]), .in_28(1'b0), .in_29(1'b0), .in_30(1'b0), .in_31(1'b0), .out(S_27));
  Multiplexer #(.Selector_Bits(5)) multiplexer_30 (
    .sel(B[4:0]), .in_0(A[28]), .in_1(A[27]), .in_2(A[26]), .in_3(A[25]), .in_4(A[24]), .in_5(A[23]),
    .in_6(A[22]), .in_7(A[21]), .in_8(A[20]), .in_9(A[19]), .in_10(A[18]), .in_11(A[17]), .in_12(A[16]),
    .in_13(A[15]), .in_14(A[14]), .in_15(A[13]), .in_16(A[12]), .in_17(A[11]), .in_18(A[10]), .in_19(A[9]),
    .in_20(A[8]), .in_21(A[7]), .in_22(A[6]), .in_23(A[5]), .in_24(A[4]), .in_25(A[3]), .in_26(A[2]),
    .in_27(A[1]), .in_28(A[0]), .in_29(1'b0), .in_30(1'b0), .in_31(1'b0), .out(S_28));
  Multiplexer #(.Selector_Bits(5)) multiplexer_31 (
    .sel(B[4:0]), .in_0(A[29]), .in_1(A[28]), .in_2(A[27]), .in_3(A[26]), .in_4(A[25]), .in_5(A[24]),
    .in_6(A[23]), .in_7(A[22]), .in_8(A[21]), .in_9(A[20]), .in_10(A[19]), .in_11(A[18]), .in_12(A[17]),
    .in_13(A[16]), .in_14(A[15]), .in_15(A[14]), .in_16(A[13]), .in_17(A[12]), .in_18(A[11]), .in_19(A[10]),
    .in_20(A[9]), .in_21(A[8]), .in_22(A[7]), .in_23(A[6]), .in_24(A[5]), .in_25(A[4]), .in_26(A[3]),
    .in_27(A[2]), .in_28(A[1]), .in_29(A[0]), .in_30(1'b0), .in_31(1'b0), .out(S_29));
  Multiplexer #(.Selector_Bits(5)) multiplexer_32 (
    .sel(B[4:0]), .in_0(A[30]), .in_1(A[29]), .in_2(A[28]), .in_3(A[27]), .in_4(A[26]), .in_5(A[25]),
    .in_6(A[24]), .in_7(A[23]), .in_8(A[22]), .in_9(A[21]), .in_10(A[20]), .in_11(A[19]), .in_12(A[18]),
    .in_13(A[17]), .in_14(A[16]), .in_15(A[15]), .in_16(A[14]), .in_17(A[13]), .in_18(A[12]), .in_19(A[11]),
    .in_20(A[10]), .in_21(A[9]), .in_22(A[8]), .in_23(A[7]), .in_24(A[6]), .in_25(A[5]), .in_26(A[4]),
    .in_27(A[3]), .in_28(A[2]), .in_29(A[1]), .in_30(A[0]), .in_31(1'b0), .out(S_30));
  Multiplexer #(.Selector_Bits(5)) multiplexer_33 (
    .sel(B[4:0]), .in_0(A[31]), .in_1(A[30]), .in_2(A[29]), .in_3(A[28]), .in_4(A[27]), .in_5(A[26]),
    .in_6(A[25]), .in_7(A[24]), .in_8(A[23]), .in_9(A[22]), .in_10(A[21]), .in_11(A[20]), .in_12(A[19]),
    .in_13(A[18]), .in_14(A[17]), .in_15(A[16]), .in_16(A[15]), .in_17(A[14]), .in_18(A[13]), .in_19(A[12]),
    .in_20(A[11]), .in_21(A[10]), .in_22(A[9]), .in_23(A[8]), .in_24(A[7]), .in_25(A[6]), .in_26(A[5]),
    .in_27(A[4]), .in_28(A[3]), .in_29(A[2]), .in_30(A[1]), .in_31(A[0]), .out(S_31));

  // Other names for the same wires on the sheet: A_0 = A[0]; A_1 = A[1]; A_2 = A[2]; A_3 = A[3]; A_4 = A[4];
  //   A_5 = A[5]; A_6 = A[6]; A_7 = A[7]; A_8 = A[8]; A_9 = A[9]; A_10 = A[10]; A_11 = A[11]; A_12 = A[12];
  //   A_13 = A[13]; A_14 = A[14]; A_15 = A[15]; A_16 = A[16]; A_17 = A[17]; A_18 = A[18]; A_19 = A[19]; A_20 = A[20];
  //   A_21 = A[21]; A_22 = A[22]; A_23 = A[23]; A_24 = A[24]; A_25 = A[25]; A_26 = A[26]; A_27 = A[27]; A_28 = A[28];
  //   A_29 = A[29]; A_30 = A[30]; A_31 = A[31]; Seletor[4:0] = B[4:0]

  // Notes on the sheet:
  //   B: número a receber shift
endmodule
