// Digital circuit teste.dig as structural Verilog
module teste (
  input  clk,
  output [31:0] Display,
  output \Tem_que_manter_o_último_display 
);

  wire and_1_out, not_1_out, not_2_out, or_1_out, sinal_de_controle_1_branch, sinal_de_controle_1_display,
       sinal_de_controle_1_halt, sinal_de_controle_1_jump, sinal_de_controle_1_ula_imm,
       sinal_de_controle_1_w_en, ula_1_zero;
  wire [2:0] sinal_de_controle_1_ula_op;
  wire [3:0] \instrução_1_a , \instrução_1_b , \instrução_1_c , \instrução_1_op ;
  wire [8:0] \Memória_de_controle_d ;
  wire [15:0] \instrução_1_const ;
  wire [31:0] banco_de_registradores_1_a, banco_de_registradores_1_b, D, ext_sign_1_out,
       \memória_de_instrução_d , multiplexer_2_out, PC_q, somador_32_bits_1_s, somador_32_bits_2_s, ula_1_s;

  not not_1 (not_1_out, clk);
  Registrador_32_bits PC (.D(D), .En(not_2_out), .CLK(not_1_out), .Q(PC_q));
  // Probe on PC_q[23:0]
  ROM #(.AddrBits(24), .isProgramMemory("true"), .Bits(32)) \memória_de_instrução  (
    .A(PC_q[23:0]), .sel(1'b1), .D(\memória_de_instrução_d ));
  // Probe on PC_q[31:24]
  Somador_32_bits somador_32_bits_1 (.A({32{1'b0}}), .B(PC_q), .C_i(1'b1), .S(somador_32_bits_1_s));  // open: C_o
  \Instrução  \instrução_1  (
    .in(\memória_de_instrução_d ), .op(\instrução_1_op ), .a(\instrução_1_a ), .b(\instrução_1_b ),
    .c(\instrução_1_c ), .\const (\instrução_1_const ));
  // Probe on somador_32_bits_1_s
  not not_2 (not_2_out, sinal_de_controle_1_halt);
  // Probe on \instrução_1_op 
  ROM #(.AddrBits(4), .isProgramMemory("true"), .Bits(9)) \Memória_de_controle  (
    .A(\instrução_1_op ), .sel(1'b1), .D(\Memória_de_controle_d ));
  Sinal_de_controle sinal_de_controle_1 (
    .in(\Memória_de_controle_d ), .W_en(sinal_de_controle_1_w_en), .Branch(sinal_de_controle_1_branch),
    .ULA_imm(sinal_de_controle_1_ula_imm), .ULA_op(sinal_de_controle_1_ula_op),
    .Display(sinal_de_controle_1_display), .Halt(sinal_de_controle_1_halt), .Jump(sinal_de_controle_1_jump));
  // Probe on \Memória_de_controle_d 
  Somador_32_bits somador_32_bits_2 (
    .A(somador_32_bits_1_s), .B(ext_sign_1_out), .C_i(1'b0), .S(somador_32_bits_2_s));  // open: C_o
  Banco_de_registradores banco_de_registradores_1 (
    .C(ula_1_s), .S_A(\instrução_1_a ), .S_B(\instrução_1_b ), .S_C(\instrução_1_c ), .CLK(clk),
    .W_En(sinal_de_controle_1_w_en), .A(banco_de_registradores_1_a), .B(banco_de_registradores_1_b));
  Ext_Sign ext_sign_1 (.In(\instrução_1_const ), .Out(ext_sign_1_out));
  Multiplexer #(.Bits(32)) multiplexer_1 (
    .sel(or_1_out), .in_0(somador_32_bits_1_s), .in_1(somador_32_bits_2_s), .out(D));
  and and_1 (and_1_out, sinal_de_controle_1_branch, ula_1_zero);
  // Probe on ext_sign_1_out
  or or_1 (or_1_out, and_1_out, sinal_de_controle_1_jump);
  // Probe on multiplexer_2_out
  Multiplexer #(.Bits(32)) multiplexer_2 (
    .sel(sinal_de_controle_1_ula_imm), .in_0(banco_de_registradores_1_b), .in_1(ext_sign_1_out),
    .out(multiplexer_2_out));
  // Probe on sinal_de_controle_1_ula_op
  ULA ula_1 (
    .A(banco_de_registradores_1_a), .B(multiplexer_2_out), .Sele(sinal_de_controle_1_ula_op), .S(ula_1_s),
    .zero(ula_1_zero));
  Registrador_32_bits u_display (
    .D(banco_de_registradores_1_a), .En(sinal_de_controle_1_display), .CLK(clk), .Q(Display));
  // Probe on ula_1_s

  assign \Tem_que_manter_o_último_display  = 1'b1;

  // Notes on the sheet:
  //   contents of memória_de_instrução (hex, n*v repeats v):
  //   1001000a,10020007,10030012,20040000,20050000,c5100007,45360000
  //   ,26260000,26440000,d4000000,95050001,b000fff9,d4000000,e0000000
  //   contents of Memória_de_controle (hex, n*v repeats v):
  //   0,a0,80,84,88,8c,90,94,98,a0,a4,160,44,2,1
endmodule
